// Logisim project Regfile-harness.circ as structural Verilog: 1 circuit, main circuit main
module main (
  output [7:0] test_num,
  output [15:0] Reg_0_Value,
  output [15:0] Reg_1_Value,
  output [15:0] Reg_2_Value,
  output [15:0] Reg_3_Value,
  output [15:0] Read_Data_1,
  output [15:0] Read_Data_2
);

  wire clock_1_out;
  wire [7:0] adder_1_out;
  wire [22:0] rom_1_data;

  Register register_1 (.D(adder_1_out), .en(1'b1), .Q(test_num), .clk(clock_1_out));  // open: clr
  Adder adder_1 (.a(8'h1), .b(test_num), .out(adder_1_out));  // open: cin, cout
  ROM #(.dataWidth(23)) rom_1 (.addr(test_num), .data(rom_1_data), .sel(1'b1));
  Clock clock_1 (.out(clock_1_out));
  Regfile_main main_1 (
    .Read_register_1(rom_1_data[1:0]), .Read_register_2(rom_1_data[3:2]), .write_register(rom_1_data[5:4]),
    .write_data(rom_1_data[21:6]), .Reg_0_Value(Reg_0_Value), .Reg_1_Value(Reg_1_Value),
    .Reg_2_Value(Reg_2_Value), .Reg_3_Value(Reg_3_Value), .RegWrite(rom_1_data[22]), .clock(clock_1_out),
    .Read_Data_1(Read_Data_1), .Read_Data_2(Read_Data_2));

  // Notes on the sheet:
  //   contents of rom_1 (hex, n*v repeats v):
  //   0 111111 111111 110111 111110
  //   There should be no blue/red wires here, and the result shouldn't be x's.
  //   YOUR REGFILE SHOULD BE FITTING HERE!
endmodule
