// Logisim project Regfile.circ as structural Verilog: 1 circuit, main circuit main
module main (
  input  [1:0] Read_register_1,
  input  [1:0] Read_register_2,
  input  [1:0] write_register,
  input  [15:0] write_data,
  input  RegWrite,
  input  clock,
  output [15:0] Reg_0_Value,
  output [15:0] Reg_1_Value,
  output [15:0] Reg_2_Value,
  output [15:0] Reg_3_Value,
  output [15:0] Read_Data_1,
  output [15:0] Read_Data_2
);

  wire and_1_out, and_2_out, and_3_out, and_4_out, and_5_out, and_6_out, and_7_out, and_8_out, not_1_out,
       not_2_out;

  not not_1 (not_1_out, write_register[0]);
  not not_2 (not_2_out, write_register[1]);
  and and_1 (and_1_out, not_1_out, not_2_out);
  and and_2 (and_2_out, write_register[0], not_2_out);
  and and_3 (and_3_out, and_1_out, RegWrite);
  and and_4 (and_4_out, and_2_out, RegWrite);
  and and_5 (and_5_out, not_1_out, write_register[1]);
  and and_6 (and_6_out, write_register[0], write_register[1]);
  and and_7 (and_7_out, and_5_out, RegWrite);
  and and_8 (and_8_out, and_6_out, RegWrite);
  Register #(.width(16)) R0 (.D(write_data), .en(and_3_out), .Q(Reg_0_Value), .clk(clock));  // open: clr
  Register #(.width(16)) R1 (.D(write_data), .en(and_4_out), .Q(Reg_1_Value), .clk(clock));  // open: clr
  Register #(.width(16)) R2 (.D(write_data), .en(and_7_out), .Q(Reg_2_Value), .clk(clock));  // open: clr
  Register #(.width(16)) R3 (.D(write_data), .en(and_8_out), .Q(Reg_3_Value), .clk(clock));  // open: clr
  Multiplexer #(.select(2), .width(16)) multiplexer_1 (
    .in0(Reg_0_Value), .in1(Reg_1_Value), .in2(Reg_2_Value), .in3(Reg_3_Value), .out(Read_Data_1),
    .sel(Read_register_1));  // open: en
  Multiplexer #(.select(2), .width(16)) multiplexer_2 (
    .in0(Reg_0_Value), .in1(Reg_1_Value), .in2(Reg_2_Value), .in3(Reg_3_Value), .out(Read_Data_2),
    .sel(Read_register_2));  // open: en

  // Notes on the sheet:
  //   These are INPUTS to the circuit
  //   These are INPUTS to the circuit
  //   These are OUTPUTS to the circuit
  //   DO NOT CHANGE THE LOCATIONS OF THE INPUTS/OUTPUTS! IF YOU DO SO, YOU NEED TO MAKE SURE THE PINS ARE AT THE RIGHT PLACE!
  //   Yet again, the clock is not an actual clock, but an input, one that will be driven from a higher circuit
  //   These are OUTPUTS to the circuit
endmodule
