// Logisim project alu.circ as structural Verilog: 2 circuits, main circuit main
module main (
  input  [15:0] X,
  input  [15:0] Y,
  input  [3:0] Switch__S,
  output Signed_Overflow,
  output [15:0] RESULT,
  output Equal
);

  wire not_1_out, not_2_out, not_3_out, or_2_out, or_3_out, overflow8_16_1_out_4, overflow8_16_2_out_4,
       overflow8_16_3_out_4, overflow8_16_4_out_4, overflow8_16_5_out_4, overflow8_16_6_out_4;
  wire [0:0] comparator_1_lt;
  wire [7:0] adder_2_out, adder_3_out, subtractor_2_out, subtractor_3_out;
  wire [15:0] adder_1_out, and_1_out, or_1_out, shifter_1_out, shifter_2_out, shifter_3_out, shifter_4_out,
       subtractor_1_out;

  Shifter #(.width(16)) shifter_1 (.in(Y), .\dist (4'b1000), .out(shifter_1_out));
  Adder #(.width(16)) adder_1 (.a(X), .b(Y), .out(adder_1_out));  // open: cin, cout
  Subtractor #(.width(16)) subtractor_1 (.a(X), .b(Y), .out(subtractor_1_out));  // open: bin, bout
  Shifter #(.width(16)) shifter_2 (.in(X), .\dist (Y[3:0]), .out(shifter_2_out));
  Shifter #(.width(16), .shift("lr")) shifter_3 (.in(X), .\dist (Y[3:0]), .out(shifter_3_out));
  Shifter #(.width(16), .shift("ar")) shifter_4 (.in(X), .\dist (Y[3:0]), .out(shifter_4_out));
  Comparator #(.width(16)) comparator_1 (.a(X), .b(Y), .lt(comparator_1_lt[0]));  // open: gt, eq
  assign or_1_out = X | Y;  // OR_Gate or_1, 16 bits wide
  assign and_1_out = X & Y;  // AND_Gate and_1, 16 bits wide
  Adder adder_2 (.a(X[7:0]), .b(Y[7:0]), .out(adder_2_out));  // open: cin, cout
  Adder adder_3 (.a(X[15:8]), .b(Y[15:8]), .out(adder_3_out));  // open: cin, cout
  Subtractor subtractor_2 (.a(X[7:0]), .b(Y[7:0]), .out(subtractor_2_out));  // open: bin, bout
  Subtractor subtractor_3 (.a(X[15:8]), .b(Y[15:8]), .out(subtractor_3_out));  // open: bin, bout
  Multiplexer #(.select(4), .width(16)) multiplexer_1 (
    .in0(adder_1_out), .in1(subtractor_1_out), .in2(shifter_2_out), .in3(shifter_3_out), .in4(shifter_4_out),
    .in5({{15{1'b0}}, comparator_1_lt[0]}), .in6(or_1_out), .in7(and_1_out),
    .in8({adder_3_out, adder_2_out}), .in9({subtractor_3_out, subtractor_2_out}), .in10(shifter_1_out),
    .in11({16{1'b0}}), .in12({16{1'b0}}), .in13({16{1'b0}}), .in14({16{1'b0}}), .in15({16{1'b0}}),
    .out(RESULT), .sel(Switch__S));  // open: en
  not not_1 (not_1_out, Y[15]);
  overflow8_16 overflow8_16_1 (.in_1(X[15]), .in_2(Y[15]), .out_4(overflow8_16_1_out_4), .in_3(adder_1_out[15]));
  overflow8_16 overflow8_16_2 (
    .in_1(X[15]), .in_2(not_1_out), .out_4(overflow8_16_2_out_4), .in_3(subtractor_1_out[15]));
  overflow8_16 overflow8_16_3 (.in_1(X[7]), .in_2(Y[7]), .out_4(overflow8_16_3_out_4), .in_3(adder_2_out[7]));
  or or_2 (or_2_out, overflow8_16_3_out_4, overflow8_16_4_out_4);
  overflow8_16 overflow8_16_4 (.in_1(X[15]), .in_2(Y[15]), .out_4(overflow8_16_4_out_4), .in_3(adder_3_out[7]));
  not not_2 (not_2_out, Y[7]);
  overflow8_16 overflow8_16_5 (.in_1(X[7]), .in_2(not_2_out), .out_4(overflow8_16_5_out_4), .in_3(subtractor_2_out[7]));
  overflow8_16 overflow8_16_6 (
    .in_1(X[15]), .in_2(not_3_out), .out_4(overflow8_16_6_out_4), .in_3(subtractor_3_out[7]));
  not not_3 (not_3_out, Y[15]);
  or or_3 (or_3_out, overflow8_16_5_out_4, overflow8_16_6_out_4);
  Multiplexer #(.select(4)) multiplexer_2 (
    .in0(overflow8_16_1_out_4), .in1(overflow8_16_2_out_4), .in2(1'b0), .in3(1'b0), .in4(1'b0), .in5(1'b0),
    .in6(1'b0), .in7(1'b0), .in8(or_2_out), .in9(or_3_out), .in10(1'b0), .in11(1'b0), .in12(1'b0),
    .in13(1'b0), .in14(1'b0), .in15(1'b0), .out(Signed_Overflow), .sel(Switch__S));  // open: en
  Comparator #(.width(16)) comparator_2 (.a(X), .b(Y), .eq(Equal));  // open: gt, lt

  // Notes on the sheet:
  //   INPUT to your circuit
  //   INPUTS to your circuit
  //   DON'T CHANGE THE INPUTS AND OUTPUTS! IF YOU DO SO, YOU NEED TO MAKE SURE THE PINS ARE IN THE RIGHT PLACES!
  //   OUTPUTS of your circuit
endmodule

module overflow8_16 (
  input  in_1,
  input  in_2,
  input  in_3,
  output out_4
);

  wire and_1_out, and_2_out, and_3_out, and_4_out, not_1_out, not_2_out, not_3_out;

  not not_1 (not_1_out, in_1);
  not not_2 (not_2_out, in_2);
  not not_3 (not_3_out, in_3);
  and and_1 (and_1_out, in_1, in_2);
  and and_2 (and_2_out, not_1_out, not_2_out);
  and and_3 (and_3_out, not_3_out, and_1_out);
  or or_1 (out_4, and_3_out, and_4_out);
  and and_4 (and_4_out, and_2_out, in_3);
endmodule
