// Logisim project cpu.circ as structural Verilog: 2 circuits, main circuit main
module main (
  input  [15:0] From_Instr_Mem,
  input  clk,
  output [15:0] r0,
  output [15:0] r1,
  output [15:0] r2,
  output [15:0] r3,
  output [15:0] Display_0,
  output [15:0] Display_1,
  output [15:0] To_Instr_Mem,
  output [15:0] Data_Mem_Data,
  output [15:0] Data_Mem_Addr,
  output Data_Mem_Write
);


  // Other names for the same wires on the sheet: d0[15:0] = Display_0; d1[15:0] = Display_1

  // Notes on the sheet:
  //   This is the current PC that you need to send as OUTPUT
  //   This is the instruction that you would receive as INPUT
  //   This is a CLK that is an INPUT driven from the harness.
  //   Remember, this circuit is loaded from the harness to be tested!
  //   DO NOT CHANGE THE LOCATIONS OF THE INPUTS OR OUTPUTS! IF YOU DO SO, YOU NEED TO MAKE SURE THE PINS ARE IN THE RIGHT PLACES!
  //   These are OUTPUTS of the circuit
  //   These are OUTPUTS of the circuit
endmodule

module DataMemory (
  input  [15:0] DataIn,
  input  [15:0] Address,
  input  RESET,
  input  clk,
  input  MemWrite,
  output [15:0] DataOut
);

  wire not_1_out;

  RAM #(.addrWidth(16), .dataWidth(16)) ram_1 (
    .addr(Address), .data(DataOut), .sel(1'b1), .clk(clk), .ld(not_1_out), .clr(RESET));
  not not_1 (not_1_out, MemWrite);
  assign DataOut = MemWrite ? DataIn : 16'bz;  // Controlled_Buffer controlled_buffer_1
endmodule
