// Logisim project cpu.circ as structural Verilog: 10 circuits, main circuit ANDControl
module main (
  input  [15:0] From_Instr_Mem,
  input  clk,
  output [15:0] r0,
  output [15:0] r1,
  output [15:0] r2,
  output [15:0] r3,
  output [15:0] Display_0,
  output [15:0] Display_1,
  output [15:0] To_Instr_Mem,
  output [15:0] Data_Mem_Data,
  output [15:0] Data_Mem_Addr,
  output Data_Mem_Write
);

  wire and_1_out, AND_2_out_3, AND_2_out_4, AND_2_out_5, AND_2_out_6, AND_2_out_7, AND_2_out_8, AND_2_out_9,
       AND_2_out_10, AND_2_out_11, AND_2_out_12, AND_2_out_13, AND_2_out_14, AND_2_out_15, AND_2_out_16,
       AND_2_out_17, AND_2_out_18, AND_2_out_19, AND_2_out_20, AND_2_out_21, AND_2_out_22, AND_2_out_23,
       AND_2_out_24, and_3_out, beq, disp, main_1_equal, not_1_out, orcontrol_1_alusrc, orcontrol_1_extop,
       orcontrol_1_jal, orcontrol_1_mem2reg, orcontrol_1_regdst, orcontrol_1_regwr;
  wire [1:0] multiplexer_2_out, multiplexer_5_out, nPCsel, npcsel_1_npcout, rtype_1_rd, rtype_1_rs,
       rtype_1_rt;
  wire [3:0] orcontrol_1_aluop, rtype_1_opcode;
  wire [5:0] rtype_1_funct;
  wire [7:0] rtype_1_immediate;
  wire [11:0] rtype_1_jaddress;
  wire [15:0] adder_2_out, bit_extender_1_out, bit_extender_2_out, imm, jumpAddr, jumpreg, main_1_result,
       multiplexer_1_out, multiplexer_3_out, multiplexer_4_out, multiplexer_6_out, multiplexer_7_out,
       multiplexer_9_out, PC_1, pipereg_1_to_ex;

  pipereg pipereg_1 (.in_1(From_Instr_Mem), .to_EX(pipereg_1_to_ex), .clk(clk), .isJump(nPCsel));
  compute_jump compute_jump_1 (.currPC(To_Instr_Mem), .jumpAddr(rtype_1_jaddress), .jump_addr(jumpAddr));
  Adder #(.width(16)) adder_1 (.a(To_Instr_Mem), .b(16'h1), .out(PC_1));  // open: cin, cout
  rtype rtype_1 (
    .instruction(pipereg_1_to_ex), .FUNCT(rtype_1_funct), .RD(rtype_1_rd), .RT(rtype_1_rt), .RS(rtype_1_rs),
    .OPCODE(rtype_1_opcode), .Immediate(rtype_1_immediate), .jAddress(rtype_1_jaddress));
  Adder #(.width(16)) adder_2 (.a(PC_1), .b(imm), .out(adder_2_out));  // open: cin, cout
  Multiplexer #(.select(2), .width(16)) multiplexer_1 (
    .in0(PC_1), .in1(adder_2_out), .in2(jumpAddr), .in3(jumpreg), .out(multiplexer_1_out),
    .sel(npcsel_1_npcout));  // open: en
  nPCsel npcsel_1 (.nPCout(npcsel_1_npcout), .nPC(nPCsel), .BEQ(beq), .equal(main_1_equal));
  not not_1 (not_1_out, rtype_1_immediate[0]);
  Register #(.width(16)) register_1 (.D(multiplexer_1_out), .en(1'b1), .Q(To_Instr_Mem), .clk(clk));  // open: clr
  Multiplexer #(.width(2)) multiplexer_2 (
    .in0(rtype_1_rd), .in1(rtype_1_rt), .out(multiplexer_2_out), .sel(orcontrol_1_regdst));  // open: en
  Multiplexer #(.width(16)) multiplexer_3 (
    .in0(Display_0), .in1(jumpreg), .out(multiplexer_3_out), .sel(and_1_out));  // open: en
  and and_1 (and_1_out, disp, not_1_out);
  ANDControl AND_2 (
    .out_5(AND_2_out_5), .out_7(AND_2_out_7), .out_9(AND_2_out_9), .out_11(AND_2_out_11),
    .out_13(AND_2_out_13), .out_15(AND_2_out_15), .out_17(AND_2_out_17), .out_19(AND_2_out_19),
    .out_21(AND_2_out_21), .out_22(AND_2_out_22), .out_23(AND_2_out_23), .out_24(AND_2_out_24),
    .OPCODE(rtype_1_opcode), .FUNCT(rtype_1_funct), .out_4(AND_2_out_4), .out_6(AND_2_out_6),
    .out_8(AND_2_out_8), .out_10(AND_2_out_10), .out_12(AND_2_out_12), .out_14(AND_2_out_14),
    .out_16(AND_2_out_16), .out_18(AND_2_out_18), .out_20(AND_2_out_20), .out_3(AND_2_out_3));
  ORControl orcontrol_1 (
    ._1(AND_2_out_5), ._2(AND_2_out_7), ._3(AND_2_out_9), ._4(AND_2_out_11), ._5(AND_2_out_13),
    ._6(AND_2_out_15), ._7(AND_2_out_17), ._8(AND_2_out_19), ._9(AND_2_out_21), ._10(AND_2_out_22),
    ._11(AND_2_out_23), ._12(AND_2_out_24), ._0(AND_2_out_3), ._1_2(AND_2_out_4), ._2_2(AND_2_out_6),
    ._3_2(AND_2_out_8), ._4_2(AND_2_out_10), ._5_2(AND_2_out_12), ._6_2(AND_2_out_14), ._7_2(AND_2_out_16),
    ._8_2(AND_2_out_18), ._9_2(AND_2_out_20), .nPCsel(nPCsel), .Mem2Reg(orcontrol_1_mem2reg),
    .MemWr(Data_Mem_Write), .ALUOp(orcontrol_1_aluop), .RegDst(orcontrol_1_regdst),
    .ALUSrc(orcontrol_1_alusrc), .ExtOP(orcontrol_1_extop), .RegWr(orcontrol_1_regwr), .beq(beq),
    .disp(disp), .jal(orcontrol_1_jal));
  Register #(.width(16)) register_2 (.D(multiplexer_3_out), .Q(Display_0), .clk(clk));  // open: en, clr
  Multiplexer #(.width(16)) multiplexer_4 (
    .in0(main_1_result), .in1(Data_Mem_Data), .out(multiplexer_4_out), .sel(orcontrol_1_mem2reg));  // open: en
  and and_3 (and_3_out, disp, rtype_1_immediate[0]);
  Multiplexer #(.width(2)) multiplexer_5 (
    .in0(multiplexer_2_out), .in1(2'b11), .out(multiplexer_5_out), .sel(orcontrol_1_jal));  // open: en
  Multiplexer #(.width(16)) multiplexer_6 (
    .in0(multiplexer_4_out), .in1(PC_1), .out(multiplexer_6_out), .sel(orcontrol_1_jal));  // open: en
  Regfile_main Register_3 (
    .Read_register_1(rtype_1_rs), .Read_register_2(rtype_1_rd), .write_register(multiplexer_5_out),
    .write_data(multiplexer_6_out), .Reg_0_Value(r0), .Reg_1_Value(r1), .Reg_2_Value(r2), .Reg_3_Value(r3),
    .RegWrite(orcontrol_1_regwr), .clock(clk), .Read_Data_1(jumpreg), .Read_Data_2(Data_Mem_Addr));
  Register #(.width(16)) register_4 (.D(multiplexer_7_out), .Q(Display_1), .clk(clk));  // open: en, clr
  Multiplexer #(.width(16)) multiplexer_7 (
    .in0(Display_1), .in1(jumpreg), .out(multiplexer_7_out), .sel(and_3_out));  // open: en
  assign bit_extender_1_out = {{8{1'b0}}, rtype_1_immediate};  // Bit_Extender bit_extender_1
  Multiplexer #(.width(16)) multiplexer_8 (
    .in0(bit_extender_1_out), .in1(bit_extender_2_out), .out(imm), .sel(orcontrol_1_extop));  // open: en
  assign bit_extender_2_out = {{8{rtype_1_immediate[7]}}, rtype_1_immediate};  // Bit_Extender bit_extender_2
  Multiplexer #(.width(16)) multiplexer_9 (
    .in0(Data_Mem_Addr), .in1(imm), .out(multiplexer_9_out), .sel(orcontrol_1_alusrc));  // open: en
  alu_main main_1 (
    .Switch__S(orcontrol_1_aluop), .X(jumpreg), .Equal(main_1_equal), .RESULT(main_1_result),
    .Y(multiplexer_9_out));  // open: Signed_Overflow
  DataMemory datamemory_1 (
    .DataIn(Data_Mem_Addr), .Address(main_1_result), .DataOut(Data_Mem_Data), .MemWrite(Data_Mem_Write),
    .clk(clk));  // open: RESET

  // Other names for the same wires on the sheet: rs[15:0] = jumpreg

  // Notes on the sheet:
  //   This is the current PC that you need to send as OUTPUT
  //   This is the instruction that you would receive as INPUT
  //   DO NOT CHANGE THE LOCATIONS OF THE INPUTS OR OUTPUTS! IF YOU DO SO, YOU NEED TO MAKE SURE THE PINS ARE IN THE RIGHT PLACES!
  //   These are OUTPUTS of the circuit
  //   rType
  //   Remember, this circuit is loaded from the harness to be tested!
  //   This is a CLK that is an INPUT driven from the harness.
  //   AND
  //   OR
  //   These are OUTPUTS of the circuit
endmodule

module DataMemory (
  input  [15:0] DataIn,
  input  [15:0] Address,
  input  RESET,
  input  clk,
  input  MemWrite,
  output [15:0] DataOut
);

  wire not_1_out;

  RAM #(.addrWidth(16), .dataWidth(16)) ram_1 (
    .addr(Address), .data(DataOut), .sel(1'b1), .clk(clk), .ld(not_1_out), .clr(RESET));
  not not_1 (not_1_out, MemWrite);
  assign DataOut = MemWrite ? DataIn : 16'bz;  // Controlled_Buffer controlled_buffer_1
endmodule

module ANDControl (
  input  [5:0] FUNCT,
  input  [3:0] OPCODE,
  output out_3,
  output out_4,
  output out_5,
  output out_6,
  output out_7,
  output out_8,
  output out_9,
  output out_10,
  output out_11,
  output out_12,
  output out_13,
  output out_14,
  output out_15,
  output out_16,
  output out_17,
  output out_18,
  output out_19,
  output out_20,
  output out_21,
  output out_22,
  output out_23,
  output out_24
);

  wire n4splitter_1_out_2, n4splitter_1_out_3, n4splitter_1_out_4, n4splitter_1_out_5, n6splitter_1_out_5,
       n6splitter_1_out_6, n6splitter_1_out_7, n6splitter_1_out_8, not_1_out, not_2_out, not_3_out,
       not_4_out, not_5_out, not_6_out, not_7_out, not_8_out, R_T_0_out;

  not not_1 (not_1_out, n4splitter_1_out_3);
  _4splitter u_4splitter_1 (
    .OPCODE(OPCODE), .out_3(n4splitter_1_out_3), .out_4(n4splitter_1_out_4), .out_5(n4splitter_1_out_5),
    .out_2(n4splitter_1_out_2));
  not not_2 (not_2_out, n4splitter_1_out_4);
  not not_3 (not_3_out, n4splitter_1_out_5);
  not not_4 (not_4_out, n4splitter_1_out_2);
  and R_T_0 (R_T_0_out, not_1_out, not_2_out, not_3_out, not_4_out);
  and JAL_1 (out_5, not_1_out, not_2_out, not_3_out, n4splitter_1_out_2);
  and J_2 (out_7, not_1_out, not_2_out, n4splitter_1_out_5, not_4_out);
  and JR_3 (out_9, not_1_out, not_2_out, n4splitter_1_out_5, n4splitter_1_out_2);
  and BEQ_4 (out_11, not_1_out, n4splitter_1_out_4, not_3_out, not_4_out);
  and ADDI_5 (out_13, not_1_out, n4splitter_1_out_4, not_3_out, n4splitter_1_out_2);
  and ANDI_6 (out_15, not_1_out, n4splitter_1_out_4, n4splitter_1_out_5, not_4_out);
  and ORI_7 (out_17, not_1_out, n4splitter_1_out_4, n4splitter_1_out_5, n4splitter_1_out_2);
  and BNE_8 (out_19, n4splitter_1_out_3, not_2_out, not_3_out, not_4_out);
  and SW_9 (out_21, n4splitter_1_out_3, not_2_out, not_3_out, n4splitter_1_out_2);
  and LUI_10 (out_22, n4splitter_1_out_3, not_2_out, n4splitter_1_out_5, not_4_out);
  and LW_11 (out_23, n4splitter_1_out_3, not_2_out, n4splitter_1_out_5, n4splitter_1_out_2);
  and DISP_12 (out_24, n4splitter_1_out_3, n4splitter_1_out_4, not_3_out, not_4_out);
  _6splitter u_6splitter_1 (
    .out_5(n6splitter_1_out_5), .out_6(n6splitter_1_out_6), .out_7(n6splitter_1_out_7),
    .out_8(n6splitter_1_out_8), .FUNCT(FUNCT), .RT(R_T_0_out));  // open: out_3, out_4
  not not_5 (not_5_out, n6splitter_1_out_5);
  not not_6 (not_6_out, n6splitter_1_out_6);
  not not_7 (not_7_out, n6splitter_1_out_7);
  not not_8 (not_8_out, n6splitter_1_out_8);
  and R_T_0_2 (out_3, not_5_out, not_6_out, not_7_out, not_8_out);
  and JAL_1_2 (out_4, not_5_out, not_6_out, not_7_out, n6splitter_1_out_8);
  and J_2_2 (out_6, not_5_out, not_6_out, n6splitter_1_out_7, not_8_out);
  and JR_3_2 (out_8, not_5_out, not_6_out, n6splitter_1_out_7, n6splitter_1_out_8);
  and BEQ_4_2 (out_10, not_5_out, n6splitter_1_out_6, not_7_out, not_8_out);
  and ADDI_5_2 (out_12, not_5_out, n6splitter_1_out_6, not_7_out, n6splitter_1_out_8);
  and ANDI_6_2 (out_14, not_5_out, n6splitter_1_out_6, n6splitter_1_out_7, not_8_out);
  and ORI_7_2 (out_16, not_5_out, n6splitter_1_out_6, n6splitter_1_out_7, n6splitter_1_out_8);
  and BNE_8_2 (out_18, n6splitter_1_out_5, not_6_out, not_7_out, not_8_out);
  and SW_9_2 (out_20, n6splitter_1_out_5, not_6_out, not_7_out, n6splitter_1_out_8);
endmodule

module ORControl (
  input  _1,
  input  _2,
  input  _3,
  input  _4,
  input  _5,
  input  _6,
  input  _7,
  input  _8,
  input  _9,
  input  _10,
  input  _11,
  input  _12,
  input  _0,
  input  _1_2,
  input  _2_2,
  input  _3_2,
  input  _4_2,
  input  _5_2,
  input  _6_2,
  input  _7_2,
  input  _8_2,
  input  _9_2,
  output jal,
  output disp,
  output beq,
  output MemWr,
  output Mem2Reg,
  output [3:0] ALUOp,
  output RegWr,
  output ExtOP,
  output ALUSrc,
  output RegDst,
  output [1:0] nPCsel
);

  wire RegWr_out;

  or nPCsel1 (nPCsel[0], _1, _2, _3);
  or nPCsel2 (nPCsel[1], _4, _8, _3);
  or u_RegDst (RegDst, _5, _6, _7, _10, _11);
  or u_ALUSrc (ALUSrc, _5, _6, _7, _9, _10, _11, _12);
  or u_ExtOP (ExtOP, _4, _5, _8, _9, _11);
  or u_RegWr (RegWr_out, _1, _2, _3, _4, _8, _9, _12);
  not not_1 (RegWr, RegWr_out);
  or ALUC3 (ALUOp[3], _8_2, _9_2, _10);
  or ALUC2 (ALUOp[2], _6, _7, _4_2, _5_2, _6_2, _7_2);
  or ALUC1 (ALUOp[1], _6, _7, _10, _2_2, _11, _3_2, _4_2, _6_2, _7_2);
  or ALUC0 (ALUOp[0], _2, _6, _1_2, _3_2, _6_2, _8_2, _9_2);

  assign beq = _4;
  assign disp = _12;
  assign jal = _1;
  assign Mem2Reg = _11;
  assign MemWr = _9;
endmodule

module _4splitter (
  input  [3:0] OPCODE,
  output out_2,
  output out_3,
  output out_4,
  output out_5
);


  assign out_2 = OPCODE[0];
  assign out_3 = OPCODE[3];
  assign out_4 = OPCODE[2];
  assign out_5 = OPCODE[1];
endmodule

module _6splitter (
  input  [5:0] FUNCT,
  input  RT,
  output out_3,
  output out_4,
  output out_5,
  output out_6,
  output out_7,
  output out_8
);

  Multiplexer #(.width(6)) multiplexer_1 (
    .in0({6{1'b1}}), .in1(FUNCT), .out({out_3, out_4, out_5, out_6, out_7, out_8}), .sel(RT));  // open: en
endmodule

module rtype (
  input  [15:0] instruction,
  output [5:0] FUNCT,
  output [1:0] RD,
  output [1:0] RT,
  output [1:0] RS,
  output [3:0] OPCODE,
  output [7:0] Immediate,
  output [11:0] jAddress
);


  assign FUNCT = instruction[5:0];
  assign Immediate = instruction[7:0];
  assign jAddress = instruction[11:0];
  assign OPCODE = instruction[15:12];
  assign RD = instruction[7:6];
  assign RS = instruction[11:10];
  assign RT = instruction[9:8];
endmodule

module compute_jump (
  input  [15:0] currPC,
  input  [11:0] jumpAddr,
  output [15:0] jump_addr
);

  wire [15:0] adder_1_out, and_1_out, bit_extender_1_out;

  Adder #(.width(16)) adder_1 (.a(currPC), .b(16'h1), .out(adder_1_out));  // open: cin, cout
  assign and_1_out = adder_1_out & 16'hf000;  // AND_Gate and_1, 16 bits wide
  assign bit_extender_1_out = {{4{1'b0}}, jumpAddr};  // Bit_Extender bit_extender_1
  assign jump_addr = and_1_out | bit_extender_1_out;  // OR_Gate or_1, 16 bits wide
endmodule

module nPCsel (
  input  [1:0] nPC,
  input  BEQ,
  input  equal,
  output [1:0] nPCout
);

  wire and_1_out, xnor_1_out;

  Multiplexer multiplexer_1 (.in0(and_1_out), .in1(nPC[0]), .out(nPCout[0]), .sel(nPC[1]));  // open: en
  and and_1 (and_1_out, nPC[0], xnor_1_out);
  xnor xnor_1 (xnor_1_out, BEQ, equal);

  assign nPCout[1] = nPC[1];
endmodule

module pipereg (
  input  [15:0] in_1,
  input  clk,
  input  [1:0] isJump,
  output [15:0] to_EX
);

  wire nand_1_out;
  wire [15:0] multiplexer_1_out;

  Multiplexer #(.width(16)) multiplexer_1 (
    .in0(in_1), .in1(16'h6), .out(multiplexer_1_out), .sel(nand_1_out));  // open: en
  Register #(.width(16)) register_1 (.D(multiplexer_1_out), .Q(to_EX), .clk(clk));  // open: en, clr
  nand nand_1 (nand_1_out, isJump[0], isJump[1]);
endmodule
